# Fritzing sketch All_In_One (saved by Fritzing 0.9.3b)
breadboards: 1

parts:
  Part2 = Arduino Uno (Rev3) - ICSP
  hc-sr1 = hc-sr04
  LCM1602_IIC3 = LCM1602 IIC [part_number="LCM1602 IIC" chip_label="LCM1602 IIC" package="DIP (Dual Inline) [THT]"]
  Part3 = Adafruit TSL2561 [part_number="Adafruit #439"]
  RHT1 = Humidity and Temperature Sensor RHT03
  LCD3 = LCD screen

nets:
  N1: Part2.A0, hc-sr1.Echo
  N2: Part2.A1, hc-sr1.Trig
  N3: Part2.A4/SDA, Part2.A5/SCL
  N4: Part2.D2, RHT1.Vcc
  VCC: Part2.5V, hc-sr1.VCC, LCM1602_IIC3.VCC, Part3.VIN, RHT1.Data-signal
  GND: Part2.GND, hc-sr1.GND, LCM1602_IIC3.GND, Part3.GND, RHT1.GND_2
  VSS: LCM1602_IIC3.VSS, LCD3.VSS
  VDD: LCM1602_IIC3.VDD, LCD3.VDD
  N5: LCM1602_IIC3.V0, LCD3.V0
  N6: LCM1602_IIC3.RS, LCD3.RS
  N7: LCM1602_IIC3.RW, LCD3.R/W
  N8: LCM1602_IIC3.E, LCD3.E
  N9: LCM1602_IIC3.D0, LCD3.DB0
  N10: LCM1602_IIC3.D1, LCD3.DB1
  N11: LCM1602_IIC3.D2, LCD3.DB2
  N12: LCM1602_IIC3.D3, LCD3.DB3
  N13: LCM1602_IIC3.D4, LCD3.DB4
  N14: LCM1602_IIC3.D5, LCD3.DB5
  N15: LCM1602_IIC3.D6, LCD3.DB6
  N16: LCM1602_IIC3.D7, LCD3.DB7
  N17: LCM1602_IIC3.A, LCD3.LED+
  N18: LCM1602_IIC3.K, LCD3.LED-
  N19: LCM1602_IIC3.SDA, Part3.SDA
  N20: LCM1602_IIC3.SCL, Part3.SCL
  N21: LCM1602_IIC3.LED_A, LCM1602_IIC3.LED_B

custom parts:
  LCM1602 IIC: I2C-Module to use a 1602 or 2004 LCD on with the wire.h libory Serial LCD Modul
  Adafruit TSL2561: The TSL2561 luminosity sensor is an advanced digital light sensor, ideal for use in a wide range of light situations. Compared to low cost CdS cells, this sensor is more precise, allowing for exact lux calculations and can be configured for different gain/timing ranges to detect light ranges from up to 0.1 - 40,000+ Lux on the fly. The best part of this sensor is that it contains both infrared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
